# Fritzing sketch NeoBot_Electronics (saved by Fritzing 0.9.3b)

parts:
  M1 = DOIT Esp32 DevKit v1 (30 pins long, 11 pins width) [part_number=ESP32S-PIN30]
  Part1 = InvenSense MPU6050
  DHT1 = DHT11 Humitidy and Temperature Sensor (3 pins)
  IC1 = MQ-2 [package="DIP (Dual Inline) [THT]"]
  L298N1 = L298N DC motor driver
  M2 = DC Motor  # not connected
  M3 = DC Motor  # not connected
  M4 = DC Motor  # not connected
  M5 = DC Motor  # not connected
  HC-SR04_Sensor_1 = HC-SR04 Ultrasonic Distance Sensor
  Squix1 = OLED 0.96" 128x64 I2C SSD1306
  Mod1 = KY-018 Photoresistor Module [package="Breakout board"]
  SERVO1 = Tower Pro SG90 servo [part_number=101246]
  J1 = Power Jack [package=power_jack_slot]  # not connected

nets:
  VCC: M1.3V3, Part1.VCC, DHT1.Plus, IC1.pin1, HC-SR04_Sensor_1.VCC, Squix1.VCC, Mod1.Vin, SERVO1.+5V
  GND: M1.GND, Part1.GND, DHT1.Gnd, IC1.pin2, HC-SR04_Sensor_1.GND, Squix1.GND, Mod1.-, SERVO1.GND
  N1: M1.D15, Mod1.S
  N2: M1.D4, DHT1.Signal
  N3: M1.D5, HC-SR04_Sensor_1.TRIG
  N4: M1.D18, HC-SR04_Sensor_1.ECHO
  N5: M1.D21, Part1.SDA, Squix1.SCA
  N6: M1.D22, Part1.SCL, Squix1.SCL
  N7: M1.D34, IC1.pin4
  N8: M1.D33, L298N1.IN4
  N9: M1.D25, L298N1.IN3
  N10: M1.D27, L298N1.IN2
  N11: M1.D14, L298N1.IN1
  N12: M1.D13, SERVO1.Signal
  N13: L298N1.5V#9, L298N1.ENA
  N14: L298N1.5V#10, L298N1.ENB

custom parts:
  DOIT Esp32 DevKit v1 (30 pins long, 11 pins width): The DOIT Esp32 DevKit v1 is one of the development board created by DOIT to evaluate the ESP-WROOM-32 module. It is based on the ESP32 microcontroller that boasts Wifi, Bluetooth, Ethernet and Low Power support all in a single chip. (vanepp) made breadboard work, adjusted pin numbering and labels and reduced size of schematic and cleaned up pcb. This chip is 30pins long (2 x15) and 11 pins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
  DHT11 Humitidy and Temperature Sensor (3 pins): DHT11 Humidity and Temperature Sensor (3 pins).
  MQ-2: MQ-2 Gas Sensor module
  L298N DC motor driver: 2x DC motor driver with 78M05 positive voltage regulator (7..35 V) L298N: max 46 V, 2 A Set 5 V Enable jumper to enable 5 V regultor (needed for the L298N) and +5 V output at screw terminal or supply external +5 V at screw terminal Set ENA and/or ENB to +5 V to enable motor permanently or supply ENA and/or ENB with PWM signal IN1 and IN2 set rotation directory for motor A (OUT1/OUT2) IN2 and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
  KY-018 Photoresistor Module: KY-018 Photoresistor module, used to measure light intensity. It can determine the presence or absence of light.
  Tower Pro SG90 servo: Original file by John De Cristofaro http://www.adafruit.com/products/1449 Adafruit Feedback Servo (Small) Edited by: e-radionica.com 28/9/2015
